// Logisim project ActualCPU.circ as structural Verilog: 2 circuits, main circuit main
module main (
);

  wire and_1_out, Clock, Halt, not_1_out, not_2_out;
  wire [7:0] Address_Counter_q, MAIN_data, pull_resistor_2_node;

  Clock clock_1 (.out(Clock));
  Counter Address_Counter (.count(Halt), .Q(Address_Counter_q));  // open: clr, load, up, clk, D, carry
  Pull_Resistor #(.pull(1)) pull_resistor_1 (.node(Halt));
  ROM MAIN (.addr(Address_Counter_q), .data(MAIN_data));
  not not_1 (not_1_out, Address_Counter_q[6]);
  and and_1 (and_1_out, Address_Counter_q[7], not_1_out);
  not not_2 (not_2_out, Address_Counter_q[7]);
  Pull_Resistor pull_resistor_2 (.node(pull_resistor_2_node[0]));
  Transistor transistor_1 (.in(MAIN_data[0]), .out(pull_resistor_2_node[0]), .gate(not_2_out));
  Pull_Resistor pull_resistor_3 (.node(pull_resistor_2_node[1]));
  Transistor transistor_2 (.in(MAIN_data[1]), .out(pull_resistor_2_node[1]), .gate(not_2_out));
  Pull_Resistor pull_resistor_4 (.node(pull_resistor_2_node[2]));
  Transistor transistor_3 (.in(MAIN_data[2]), .out(pull_resistor_2_node[2]), .gate(not_2_out));
  RAM #(.databus("bidir")) ram_1 (
    .addr(Address_Counter_q), .oe(and_1_out), .clk(Clock), .data(pull_resistor_2_node));  // open: we
  Pull_Resistor pull_resistor_5 (.node(pull_resistor_2_node));
  Pull_Resistor pull_resistor_6 (.node(pull_resistor_2_node[3]));
  Transistor transistor_4 (.in(MAIN_data[3]), .out(pull_resistor_2_node[3]), .gate(not_2_out));
  Pull_Resistor pull_resistor_7 (.node(pull_resistor_2_node[4]));
  Transistor transistor_5 (.in(MAIN_data[4]), .out(pull_resistor_2_node[4]), .gate(not_2_out));
  Pull_Resistor pull_resistor_8 (.node(pull_resistor_2_node[5]));
  Transistor transistor_6 (.in(MAIN_data[5]), .out(pull_resistor_2_node[5]), .gate(not_2_out));
  Pull_Resistor pull_resistor_9 (.node(pull_resistor_2_node[6]));
  Transistor transistor_7 (.in(MAIN_data[6]), .out(pull_resistor_2_node[6]), .gate(not_2_out));
  Pull_Resistor pull_resistor_10 (.node(pull_resistor_2_node[7]));
  Transistor transistor_8 (.in(MAIN_data[7]), .out(pull_resistor_2_node[7]), .gate(not_2_out));
  PLA #(.in_width(8), .out_width(16), .\table ("00000001 1000000001011110 # Load A From Address\n00000010 1000000000010001 # Load Int to A\n00000000 0000000000000000")) MICROCODE (.in(pull_resistor_2_node));  // open: out
  Register JMP (.D(pull_resistor_2_node));  // open: en, clk, Q, clr
  Register A (.D(pull_resistor_2_node));  // open: en, clk, Q, clr
  Register B (.D(pull_resistor_2_node));  // open: en, clk, Q, clr

  // Notes on the sheet:
  //   contents of MAIN (hex, n*v repeats v):
  //   1 aa
  //   ROM OUTPUT ENABLE
  //   ROM OUT
  //   RAM OUT
endmodule

module program_counter (
);

  Counter counter_1 ();  // open: clr, load, up, count, clk, D, carry, Q
endmodule
